// Logisim project Difference-engine.circ as structural Verilog: 11 circuits, main circuit main
module main (
  input  in_1,
  input  in_2,
  input  in_3,
  input  in_4,
  input  in_5,
  input  in_6,
  input  in_7,
  input  in_8,
  input  in_9,
  input  in_10,
  input  in_11,
  input  in_12,
  input  in_13,
  input  in_14,
  input  in_15,
  input  in_16,
  input  in_17,
  input  in_18,
  input  in_19,
  input  in_20,
  input  in_21,
  input  in_22,
  input  in_23,
  input  in_24,
  input  in_25,
  input  in_26,
  input  in_27,
  input  in_28,
  input  in_29,
  input  in_30,
  input  in_31,
  input  in_32,
  input  in_33,
  input  in_34,
  input  in_35,
  input  in_36,
  input  in_37,
  input  in_38,
  input  in_39,
  input  in_40,
  input  in_41,
  input  in_42,
  input  in_43,
  input  in_44,
  input  in_45,
  input  in_46,
  input  in_47,
  input  in_48,
  input  in_49,
  input  in_50,
  input  in_51,
  input  in_52,
  input  in_53,
  input  in_54,
  output out_55,
  output out_56,
  output out_57,
  output out_58,
  output out_59,
  output out_60,
  output out_61,
  output out_62,
  output out_63,
  output out_64,
  output out_65,
  output out_66,
  output out_67,
  output out_68,
  output out_69,
  output out_70,
  output out_71
);

  wire buffer_1_out, buffer_2_out, buffer_3_out, buffer_4_out, buffer_5_out, buffer_6_out, buffer_7_out,
       buffer_8_out, buffer_9_out, buffer_10_out, n16_bit_registers_1_out_36, n16_bit_registers_1_out_37,
       n16_bit_registers_1_out_38, n16_bit_registers_1_out_39, n16_bit_registers_1_out_40,
       n16_bit_registers_1_out_41, n16_bit_registers_1_out_42, n16_bit_registers_1_out_43,
       n16_bit_registers_1_out_44, n16_bit_registers_1_out_45, n16_bit_registers_1_out_46,
       n16_bit_registers_1_out_47, n16_bit_registers_1_out_48, n16_bit_registers_1_out_49,
       n16_bit_registers_1_out_50, n16_bit_registers_1_out_51, n16_bit_registers_2_out_36,
       n16_bit_registers_2_out_37, n16_bit_registers_2_out_38, n16_bit_registers_2_out_39,
       n16_bit_registers_2_out_40, n16_bit_registers_2_out_41, n16_bit_registers_2_out_42,
       n16_bit_registers_2_out_43, n16_bit_registers_2_out_44, n16_bit_registers_2_out_45,
       n16_bit_registers_2_out_46, n16_bit_registers_2_out_47, n16_bit_registers_2_out_48,
       n16_bit_registers_2_out_49, n16_bit_registers_2_out_50, n16_bit_registers_2_out_51,
       n16_bit_total_adder_1_out_36, n16_bit_total_adder_1_out_37, n16_bit_total_adder_1_out_38,
       n16_bit_total_adder_1_out_39, n16_bit_total_adder_1_out_40, n16_bit_total_adder_1_out_41,
       n16_bit_total_adder_1_out_42, n16_bit_total_adder_1_out_43, n16_bit_total_adder_1_out_44,
       n16_bit_total_adder_1_out_45, n16_bit_total_adder_1_out_46, n16_bit_total_adder_1_out_47,
       n16_bit_total_adder_1_out_48, n16_bit_total_adder_1_out_49, n16_bit_total_adder_1_out_50,
       n16_bit_total_adder_1_out_51, n16_bit_total_adder_2_out_36, n16_bit_total_adder_2_out_37,
       n16_bit_total_adder_2_out_38, n16_bit_total_adder_2_out_39, n16_bit_total_adder_2_out_40,
       n16_bit_total_adder_2_out_41, n16_bit_total_adder_2_out_42, n16_bit_total_adder_2_out_43,
       n16_bit_total_adder_2_out_44, n16_bit_total_adder_2_out_45, n16_bit_total_adder_2_out_46,
       n16_bit_total_adder_2_out_47, n16_bit_total_adder_2_out_48, n16_bit_total_adder_2_out_49,
       n16_bit_total_adder_2_out_50, n16_bit_total_adder_2_out_51, or_1_out, or_2_out, parser_1_out_7,
       parser_1_out_8, parser_1_out_9, parser_1_out_10, parser_1_out_11, parser_1_out_12, parser_1_out_13,
       parser_1_out_14;

  _16_bit_registers u_16_bit_registers_1 (
    .in_17(in_33), .in_20(buffer_1_out), .in_19(in_35), .in_21(in_36), .in_22(in_37), .in_23(in_38),
    .in_24(in_39), .in_25(in_40), .in_26(in_41), .in_27(in_42), .in_28(in_43), .in_29(in_44), .in_30(in_45),
    .in_31(in_46), .in_32(in_47), .in_33(in_48), .in_34(in_49), .in_35(parser_1_out_7),
    .out_36(n16_bit_registers_1_out_36), .out_37(n16_bit_registers_1_out_37),
    .out_38(n16_bit_registers_1_out_38), .out_39(n16_bit_registers_1_out_39),
    .out_40(n16_bit_registers_1_out_40), .out_41(n16_bit_registers_1_out_41),
    .out_42(n16_bit_registers_1_out_42), .out_43(n16_bit_registers_1_out_43),
    .out_44(n16_bit_registers_1_out_44), .out_45(n16_bit_registers_1_out_45),
    .out_46(n16_bit_registers_1_out_46), .out_47(n16_bit_registers_1_out_47),
    .out_48(n16_bit_registers_1_out_48), .out_49(n16_bit_registers_1_out_49),
    .out_50(n16_bit_registers_1_out_50), .out_51(n16_bit_registers_1_out_51), .in_18(in_34));  // open: in_1, in_2, in_3, in_4, in_5, in_6, in_7, in_8, in_9, in_10, in_11, in_12, in_13, in_14, in_15, in_16
  buf buffer_1 (buffer_1_out, parser_1_out_10);
  _16_bit_total_adder u_16_bit_total_adder_1 (
    .out_35(out_70), .in_1(n16_bit_registers_1_out_36), .in_2(n16_bit_registers_1_out_37),
    .in_3(n16_bit_registers_1_out_38), .in_4(n16_bit_registers_1_out_39), .in_5(n16_bit_registers_1_out_40),
    .in_6(n16_bit_registers_1_out_41), .in_7(n16_bit_registers_1_out_42), .in_8(n16_bit_registers_1_out_43),
    .in_9(n16_bit_registers_1_out_44), .in_10(n16_bit_registers_1_out_45),
    .in_11(n16_bit_registers_1_out_46), .in_12(n16_bit_registers_1_out_47),
    .in_13(n16_bit_registers_1_out_48), .in_14(n16_bit_registers_1_out_49),
    .in_15(n16_bit_registers_1_out_50), .in_16(n16_bit_registers_1_out_51),
    .in_17(n16_bit_registers_2_out_36), .in_18(n16_bit_registers_2_out_37),
    .in_19(n16_bit_registers_2_out_38), .in_20(n16_bit_registers_2_out_39),
    .in_21(n16_bit_registers_2_out_40), .in_22(n16_bit_registers_2_out_41),
    .in_23(n16_bit_registers_2_out_42), .in_24(n16_bit_registers_2_out_43),
    .in_25(n16_bit_registers_2_out_44), .in_26(n16_bit_registers_2_out_45),
    .in_27(n16_bit_registers_2_out_46), .in_28(n16_bit_registers_2_out_47),
    .in_29(n16_bit_registers_2_out_48), .in_30(n16_bit_registers_2_out_49),
    .in_31(n16_bit_registers_2_out_50), .in_32(n16_bit_registers_2_out_51), .in_33(buffer_2_out),
    .out_36(n16_bit_total_adder_1_out_36), .out_37(n16_bit_total_adder_1_out_37),
    .out_38(n16_bit_total_adder_1_out_38), .out_39(n16_bit_total_adder_1_out_39),
    .out_40(n16_bit_total_adder_1_out_40), .out_41(n16_bit_total_adder_1_out_41),
    .out_42(n16_bit_total_adder_1_out_42), .out_43(n16_bit_total_adder_1_out_43),
    .out_44(n16_bit_total_adder_1_out_44), .out_45(n16_bit_total_adder_1_out_45),
    .out_46(n16_bit_total_adder_1_out_46), .out_47(n16_bit_total_adder_1_out_47),
    .out_48(n16_bit_total_adder_1_out_48), .out_49(n16_bit_total_adder_1_out_49),
    .out_50(n16_bit_total_adder_1_out_50), .out_51(n16_bit_total_adder_1_out_51), .in_34(buffer_3_out));
  buf buffer_2 (buffer_2_out, parser_1_out_10);
  buf buffer_3 (buffer_3_out, parser_1_out_11);
  buf buffer_4 (buffer_4_out, parser_1_out_10);
  buf buffer_5 (buffer_5_out, parser_1_out_11);
  parser parser_1 (
    .in_1(in_51), .in_2(in_52), .in_3(in_53), .in_4(in_54), .in_5(in_50), .out_7(parser_1_out_7),
    .out_8(parser_1_out_8), .out_9(parser_1_out_9), .out_10(parser_1_out_10), .out_11(parser_1_out_11),
    .out_12(parser_1_out_12), .out_13(parser_1_out_13), .out_14(parser_1_out_14));  // open: out_6, out_15, out_16, out_17
  _16_bit_registers u_16_bit_registers_2 (
    .in_1(in_1), .in_2(in_2), .in_3(in_3), .in_4(in_4), .in_5(in_5), .in_6(in_6), .in_7(in_7), .in_8(in_8),
    .in_9(in_9), .in_10(in_10), .in_11(in_11), .in_12(in_12), .in_13(in_13), .in_14(in_14), .in_15(in_15),
    .in_16(in_16), .in_17(parser_1_out_8), .in_20(or_1_out), .in_19(n16_bit_total_adder_1_out_37),
    .in_21(n16_bit_total_adder_1_out_38), .in_22(n16_bit_total_adder_1_out_39),
    .in_23(n16_bit_total_adder_1_out_40), .in_24(n16_bit_total_adder_1_out_41),
    .in_25(n16_bit_total_adder_1_out_42), .in_26(n16_bit_total_adder_1_out_43),
    .in_27(n16_bit_total_adder_1_out_44), .in_28(n16_bit_total_adder_1_out_45),
    .in_29(n16_bit_total_adder_1_out_46), .in_30(n16_bit_total_adder_1_out_47),
    .in_31(n16_bit_total_adder_1_out_48), .in_32(n16_bit_total_adder_1_out_49),
    .in_33(n16_bit_total_adder_1_out_50), .in_34(n16_bit_total_adder_1_out_51), .in_35(buffer_5_out),
    .out_36(n16_bit_registers_2_out_36), .out_37(n16_bit_registers_2_out_37),
    .out_38(n16_bit_registers_2_out_38), .out_39(n16_bit_registers_2_out_39),
    .out_40(n16_bit_registers_2_out_40), .out_41(n16_bit_registers_2_out_41),
    .out_42(n16_bit_registers_2_out_42), .out_43(n16_bit_registers_2_out_43),
    .out_44(n16_bit_registers_2_out_44), .out_45(n16_bit_registers_2_out_45),
    .out_46(n16_bit_registers_2_out_46), .out_47(n16_bit_registers_2_out_47),
    .out_48(n16_bit_registers_2_out_48), .out_49(n16_bit_registers_2_out_49),
    .out_50(n16_bit_registers_2_out_50), .out_51(n16_bit_registers_2_out_51),
    .in_18(n16_bit_total_adder_1_out_36));
  or or_1 (or_1_out, buffer_4_out, buffer_6_out);
  buf buffer_6 (buffer_6_out, parser_1_out_12);
  _16_bit_total_adder u_16_bit_total_adder_2 (
    .in_1(n16_bit_registers_2_out_36), .in_2(n16_bit_registers_2_out_37), .in_3(n16_bit_registers_2_out_38),
    .in_4(n16_bit_registers_2_out_39), .in_5(n16_bit_registers_2_out_40), .in_6(n16_bit_registers_2_out_41),
    .in_7(n16_bit_registers_2_out_42), .in_8(n16_bit_registers_2_out_43), .in_9(n16_bit_registers_2_out_44),
    .in_10(n16_bit_registers_2_out_45), .in_11(n16_bit_registers_2_out_46),
    .in_12(n16_bit_registers_2_out_47), .in_13(n16_bit_registers_2_out_48),
    .in_14(n16_bit_registers_2_out_49), .in_15(n16_bit_registers_2_out_50),
    .in_16(n16_bit_registers_2_out_51), .in_17(out_55), .in_18(out_56), .in_19(out_57), .in_20(out_58),
    .in_21(out_59), .in_22(out_60), .in_23(out_61), .in_24(out_62), .in_25(out_63), .in_26(out_64),
    .in_27(out_65), .in_28(out_66), .in_29(out_67), .in_30(out_68), .in_31(out_69), .in_32(out_71),
    .in_33(buffer_7_out), .out_36(n16_bit_total_adder_2_out_36), .out_37(n16_bit_total_adder_2_out_37),
    .out_38(n16_bit_total_adder_2_out_38), .out_39(n16_bit_total_adder_2_out_39),
    .out_40(n16_bit_total_adder_2_out_40), .out_41(n16_bit_total_adder_2_out_41),
    .out_42(n16_bit_total_adder_2_out_42), .out_43(n16_bit_total_adder_2_out_43),
    .out_44(n16_bit_total_adder_2_out_44), .out_45(n16_bit_total_adder_2_out_45),
    .out_46(n16_bit_total_adder_2_out_46), .out_47(n16_bit_total_adder_2_out_47),
    .out_48(n16_bit_total_adder_2_out_48), .out_49(n16_bit_total_adder_2_out_49),
    .out_50(n16_bit_total_adder_2_out_50), .out_51(n16_bit_total_adder_2_out_51), .in_34(buffer_8_out));  // open: out_35
  buf buffer_7 (buffer_7_out, parser_1_out_12);
  buf buffer_8 (buffer_8_out, parser_1_out_13);
  buf buffer_9 (buffer_9_out, parser_1_out_12);
  buf buffer_10 (buffer_10_out, parser_1_out_13);
  _16_bit_registers u_16_bit_registers_3 (
    .in_1(in_17), .in_2(in_18), .in_3(in_19), .in_4(in_20), .in_5(in_21), .in_6(in_22), .in_7(in_23),
    .in_8(in_24), .in_9(in_25), .in_10(in_26), .in_11(in_27), .in_12(in_28), .in_13(in_29), .in_14(in_30),
    .in_15(in_31), .in_16(in_32), .in_17(parser_1_out_9), .in_20(or_2_out),
    .in_19(n16_bit_total_adder_2_out_37), .in_21(n16_bit_total_adder_2_out_38),
    .in_22(n16_bit_total_adder_2_out_39), .in_23(n16_bit_total_adder_2_out_40),
    .in_24(n16_bit_total_adder_2_out_41), .in_25(n16_bit_total_adder_2_out_42),
    .in_26(n16_bit_total_adder_2_out_43), .in_27(n16_bit_total_adder_2_out_44),
    .in_28(n16_bit_total_adder_2_out_45), .in_29(n16_bit_total_adder_2_out_46),
    .in_30(n16_bit_total_adder_2_out_47), .in_31(n16_bit_total_adder_2_out_48),
    .in_32(n16_bit_total_adder_2_out_49), .in_33(n16_bit_total_adder_2_out_50),
    .in_34(n16_bit_total_adder_2_out_51), .in_35(buffer_10_out), .out_36(out_55), .out_37(out_56),
    .out_38(out_57), .out_39(out_58), .out_40(out_59), .out_41(out_60), .out_42(out_61), .out_43(out_62),
    .out_44(out_63), .out_45(out_64), .out_46(out_65), .out_47(out_66), .out_48(out_67), .out_49(out_68),
    .out_50(out_69), .out_51(out_71), .in_18(n16_bit_total_adder_2_out_36));
  or or_2 (or_2_out, buffer_9_out, parser_1_out_14);
endmodule

module RS_Trigger (
  input  in_1,
  input  in_2,
  output out_3,
  output out_4
);

  wire or_1_out, or_2_out;

  or or_1 (or_1_out, in_1, out_4);
  or or_2 (or_2_out, out_3, in_2);
  not not_1 (out_3, or_1_out);
  not not_2 (out_4, or_2_out);
endmodule

module latch__electronic (
  input  in_1,
  output out_2
);

  wire buffer_1_out, not_1_out;

  buf buffer_1 (buffer_1_out, in_1);
  not not_1 (not_1_out, in_1);
  RS_Trigger rs_trigger_1 (.in_1(buffer_1_out), .in_2(not_1_out), .out_4(out_2));  // open: out_3
endmodule

module D_Trigger (
  input  in_1,
  input  in_2,
  output out_3
);

  wire and_1_out, and_2_out, buffer_1_out, buffer_2_out, not_1_out;

  buf buffer_1 (buffer_1_out, in_1);
  buf buffer_2 (buffer_2_out, in_2);
  not not_1 (not_1_out, in_1);
  and and_1 (and_1_out, buffer_1_out, buffer_2_out);
  and and_2 (and_2_out, buffer_2_out, not_1_out);
  RS_Trigger rs_trigger_1 (.in_1(and_1_out), .in_2(and_2_out), .out_4(out_3));  // open: out_3
endmodule

module D_flip_flop_with_output_control (
  input  in_1,
  input  in_2,
  input  in_3,
  output out_4
);

  wire and_1_out, and_2_out, buffer_1_out, buffer_2_out, not_1_out, rs_trigger_1_out_4;

  buf buffer_1 (buffer_1_out, in_2);
  buf buffer_2 (buffer_2_out, in_1);
  not not_1 (not_1_out, in_1);
  and and_1 (and_1_out, buffer_2_out, buffer_1_out);
  and and_2 (and_2_out, buffer_1_out, not_1_out);
  RS_Trigger rs_trigger_1 (.in_1(and_1_out), .in_2(and_2_out), .out_4(rs_trigger_1_out_4));  // open: out_3
  and and_3 (out_4, rs_trigger_1_out_4, in_3);
endmodule

module _16_bit_registers (
  input  in_1,
  input  in_2,
  input  in_3,
  input  in_4,
  input  in_5,
  input  in_6,
  input  in_7,
  input  in_8,
  input  in_9,
  input  in_10,
  input  in_11,
  input  in_12,
  input  in_13,
  input  in_14,
  input  in_15,
  input  in_16,
  input  in_17,
  input  in_18,
  input  in_19,
  input  in_20,
  input  in_21,
  input  in_22,
  input  in_23,
  input  in_24,
  input  in_25,
  input  in_26,
  input  in_27,
  input  in_28,
  input  in_29,
  input  in_30,
  input  in_31,
  input  in_32,
  input  in_33,
  input  in_34,
  input  in_35,
  output out_36,
  output out_37,
  output out_38,
  output out_39,
  output out_40,
  output out_41,
  output out_42,
  output out_43,
  output out_44,
  output out_45,
  output out_46,
  output out_47,
  output out_48,
  output out_49,
  output out_50,
  output out_51
);

  wire controlled_buffer_1_out, controlled_buffer_2_out, controlled_buffer_3_out, controlled_buffer_4_out,
       controlled_buffer_5_out, controlled_buffer_6_out, controlled_buffer_7_out, controlled_buffer_8_out,
       controlled_buffer_9_out, controlled_buffer_10_out, controlled_buffer_11_out, controlled_buffer_12_out,
       controlled_buffer_13_out, controlled_buffer_14_out, controlled_buffer_15_out,
       controlled_buffer_16_out, d_trigger_1_out_3, d_trigger_2_out_3, d_trigger_3_out_3, d_trigger_4_out_3,
       d_trigger_5_out_3, d_trigger_6_out_3, d_trigger_7_out_3, d_trigger_8_out_3, d_trigger_9_out_3,
       d_trigger_10_out_3, d_trigger_11_out_3, d_trigger_12_out_3, d_trigger_13_out_3, d_trigger_14_out_3,
       d_trigger_15_out_3, d_trigger_16_out_3, d_trigger_17_out_3, d_trigger_18_out_3, d_trigger_19_out_3,
       d_trigger_20_out_3, d_trigger_21_out_3, d_trigger_22_out_3, d_trigger_23_out_3, d_trigger_24_out_3,
       d_trigger_25_out_3, d_trigger_26_out_3, d_trigger_27_out_3, d_trigger_28_out_3, d_trigger_29_out_3,
       d_trigger_30_out_3, d_trigger_31_out_3, d_trigger_32_out_3, or_1_out;

  assign controlled_buffer_1_out = in_17 ? d_trigger_1_out_3 : 1'bz;  // Controlled_Buffer controlled_buffer_1
  D_Trigger d_trigger_1 (.in_1(in_1), .in_2(in_17), .out_3(d_trigger_1_out_3));
  assign controlled_buffer_2_out = in_17 ? d_trigger_2_out_3 : 1'bz;  // Controlled_Buffer controlled_buffer_2
  D_Trigger d_trigger_2 (.in_1(in_2), .in_2(in_17), .out_3(d_trigger_2_out_3));
  assign controlled_buffer_3_out = in_17 ? d_trigger_3_out_3 : 1'bz;  // Controlled_Buffer controlled_buffer_3
  D_Trigger d_trigger_3 (.in_1(in_3), .in_2(in_17), .out_3(d_trigger_3_out_3));
  assign controlled_buffer_4_out = in_17 ? d_trigger_4_out_3 : 1'bz;  // Controlled_Buffer controlled_buffer_4
  D_Trigger d_trigger_4 (.in_1(in_4), .in_2(in_17), .out_3(d_trigger_4_out_3));
  assign controlled_buffer_5_out = in_17 ? d_trigger_5_out_3 : 1'bz;  // Controlled_Buffer controlled_buffer_5
  D_Trigger d_trigger_5 (.in_1(in_5), .in_2(in_17), .out_3(d_trigger_5_out_3));
  assign controlled_buffer_6_out = in_17 ? d_trigger_6_out_3 : 1'bz;  // Controlled_Buffer controlled_buffer_6
  D_Trigger d_trigger_6 (.in_1(in_6), .in_2(in_17), .out_3(d_trigger_6_out_3));
  assign controlled_buffer_7_out = in_17 ? d_trigger_7_out_3 : 1'bz;  // Controlled_Buffer controlled_buffer_7
  D_Trigger d_trigger_7 (.in_1(in_7), .in_2(in_17), .out_3(d_trigger_7_out_3));
  assign controlled_buffer_8_out = in_17 ? d_trigger_8_out_3 : 1'bz;  // Controlled_Buffer controlled_buffer_8
  D_Trigger d_trigger_8 (.in_1(in_8), .in_2(in_17), .out_3(d_trigger_8_out_3));
  assign controlled_buffer_9_out = in_17 ? d_trigger_9_out_3 : 1'bz;  // Controlled_Buffer controlled_buffer_9
  D_Trigger d_trigger_9 (.in_1(in_9), .in_2(in_17), .out_3(d_trigger_9_out_3));
  assign controlled_buffer_10_out = in_17 ? d_trigger_10_out_3 : 1'bz;  // Controlled_Buffer controlled_buffer_10
  D_Trigger d_trigger_10 (.in_1(in_10), .in_2(in_17), .out_3(d_trigger_10_out_3));
  assign controlled_buffer_11_out = in_17 ? d_trigger_11_out_3 : 1'bz;  // Controlled_Buffer controlled_buffer_11
  D_Trigger d_trigger_11 (.in_1(in_11), .in_2(in_17), .out_3(d_trigger_11_out_3));
  assign controlled_buffer_12_out = in_17 ? d_trigger_12_out_3 : 1'bz;  // Controlled_Buffer controlled_buffer_12
  D_Trigger d_trigger_12 (.in_1(in_12), .in_2(in_17), .out_3(d_trigger_12_out_3));
  assign controlled_buffer_13_out = in_17 ? d_trigger_13_out_3 : 1'bz;  // Controlled_Buffer controlled_buffer_13
  D_Trigger d_trigger_13 (.in_1(in_13), .in_2(in_17), .out_3(d_trigger_13_out_3));
  assign controlled_buffer_14_out = in_17 ? d_trigger_14_out_3 : 1'bz;  // Controlled_Buffer controlled_buffer_14
  D_Trigger d_trigger_14 (.in_1(in_14), .in_2(in_17), .out_3(d_trigger_14_out_3));
  assign controlled_buffer_15_out = in_17 ? d_trigger_15_out_3 : 1'bz;  // Controlled_Buffer controlled_buffer_15
  D_Trigger d_trigger_15 (.in_1(in_15), .in_2(in_17), .out_3(d_trigger_15_out_3));
  assign controlled_buffer_16_out = in_17 ? d_trigger_16_out_3 : 1'bz;  // Controlled_Buffer controlled_buffer_16
  D_Trigger d_trigger_16 (.in_1(in_16), .in_2(in_17), .out_3(d_trigger_16_out_3));
  assign controlled_buffer_1_out = in_35 ? d_trigger_17_out_3 : 1'bz;  // Controlled_Buffer controlled_buffer_17
  D_Trigger d_trigger_17 (.in_1(in_18), .in_2(in_35), .out_3(d_trigger_17_out_3));
  assign controlled_buffer_2_out = in_35 ? d_trigger_18_out_3 : 1'bz;  // Controlled_Buffer controlled_buffer_18
  D_Trigger d_trigger_18 (.in_1(in_19), .in_2(in_35), .out_3(d_trigger_18_out_3));
  assign controlled_buffer_3_out = in_35 ? d_trigger_19_out_3 : 1'bz;  // Controlled_Buffer controlled_buffer_19
  D_Trigger d_trigger_19 (.in_1(in_21), .in_2(in_35), .out_3(d_trigger_19_out_3));
  assign controlled_buffer_4_out = in_35 ? d_trigger_20_out_3 : 1'bz;  // Controlled_Buffer controlled_buffer_20
  D_Trigger d_trigger_20 (.in_1(in_22), .in_2(in_35), .out_3(d_trigger_20_out_3));
  assign controlled_buffer_5_out = in_35 ? d_trigger_21_out_3 : 1'bz;  // Controlled_Buffer controlled_buffer_21
  D_Trigger d_trigger_21 (.in_1(in_23), .in_2(in_35), .out_3(d_trigger_21_out_3));
  assign controlled_buffer_6_out = in_35 ? d_trigger_22_out_3 : 1'bz;  // Controlled_Buffer controlled_buffer_22
  D_Trigger d_trigger_22 (.in_1(in_24), .in_2(in_35), .out_3(d_trigger_22_out_3));
  assign controlled_buffer_7_out = in_35 ? d_trigger_23_out_3 : 1'bz;  // Controlled_Buffer controlled_buffer_23
  D_Trigger d_trigger_23 (.in_1(in_25), .in_2(in_35), .out_3(d_trigger_23_out_3));
  assign controlled_buffer_8_out = in_35 ? d_trigger_24_out_3 : 1'bz;  // Controlled_Buffer controlled_buffer_24
  D_Trigger d_trigger_24 (.in_1(in_26), .in_2(in_35), .out_3(d_trigger_24_out_3));
  assign controlled_buffer_9_out = in_35 ? d_trigger_25_out_3 : 1'bz;  // Controlled_Buffer controlled_buffer_25
  D_Trigger d_trigger_25 (.in_1(in_27), .in_2(in_35), .out_3(d_trigger_25_out_3));
  assign controlled_buffer_10_out = in_35 ? d_trigger_26_out_3 : 1'bz;  // Controlled_Buffer controlled_buffer_26
  D_Trigger d_trigger_26 (.in_1(in_28), .in_2(in_35), .out_3(d_trigger_26_out_3));
  assign controlled_buffer_11_out = in_35 ? d_trigger_27_out_3 : 1'bz;  // Controlled_Buffer controlled_buffer_27
  D_Trigger d_trigger_27 (.in_1(in_29), .in_2(in_35), .out_3(d_trigger_27_out_3));
  assign controlled_buffer_12_out = in_35 ? d_trigger_28_out_3 : 1'bz;  // Controlled_Buffer controlled_buffer_28
  D_Trigger d_trigger_28 (.in_1(in_30), .in_2(in_35), .out_3(d_trigger_28_out_3));
  assign controlled_buffer_13_out = in_35 ? d_trigger_29_out_3 : 1'bz;  // Controlled_Buffer controlled_buffer_29
  D_Trigger d_trigger_29 (.in_1(in_31), .in_2(in_35), .out_3(d_trigger_29_out_3));
  assign controlled_buffer_14_out = in_35 ? d_trigger_30_out_3 : 1'bz;  // Controlled_Buffer controlled_buffer_30
  D_Trigger d_trigger_30 (.in_1(in_32), .in_2(in_35), .out_3(d_trigger_30_out_3));
  assign controlled_buffer_15_out = in_35 ? d_trigger_31_out_3 : 1'bz;  // Controlled_Buffer controlled_buffer_31
  D_Trigger d_trigger_31 (.in_1(in_33), .in_2(in_35), .out_3(d_trigger_31_out_3));
  assign controlled_buffer_16_out = in_35 ? d_trigger_32_out_3 : 1'bz;  // Controlled_Buffer controlled_buffer_32
  D_Trigger d_trigger_32 (.in_1(in_34), .in_2(in_35), .out_3(d_trigger_32_out_3));
  or or_1 (or_1_out, in_17, in_35);
  D_flip_flop_with_output_control d_flip_flop_with_output_control_1 (
    .in_1(controlled_buffer_1_out), .in_3(in_20), .out_4(out_36), .in_2(or_1_out));
  D_flip_flop_with_output_control d_flip_flop_with_output_control_2 (
    .in_1(controlled_buffer_2_out), .in_3(in_20), .out_4(out_37), .in_2(or_1_out));
  D_flip_flop_with_output_control d_flip_flop_with_output_control_3 (
    .in_1(controlled_buffer_3_out), .in_3(in_20), .out_4(out_38), .in_2(or_1_out));
  D_flip_flop_with_output_control d_flip_flop_with_output_control_4 (
    .in_1(controlled_buffer_4_out), .in_3(in_20), .out_4(out_39), .in_2(or_1_out));
  D_flip_flop_with_output_control d_flip_flop_with_output_control_5 (
    .in_1(controlled_buffer_5_out), .in_3(in_20), .out_4(out_40), .in_2(or_1_out));
  D_flip_flop_with_output_control d_flip_flop_with_output_control_6 (
    .in_1(controlled_buffer_6_out), .in_3(in_20), .out_4(out_41), .in_2(or_1_out));
  D_flip_flop_with_output_control d_flip_flop_with_output_control_7 (
    .in_1(controlled_buffer_7_out), .in_3(in_20), .out_4(out_42), .in_2(or_1_out));
  D_flip_flop_with_output_control d_flip_flop_with_output_control_8 (
    .in_1(controlled_buffer_8_out), .in_3(in_20), .out_4(out_43), .in_2(or_1_out));
  D_flip_flop_with_output_control d_flip_flop_with_output_control_9 (
    .in_1(controlled_buffer_9_out), .in_3(in_20), .out_4(out_44), .in_2(or_1_out));
  D_flip_flop_with_output_control d_flip_flop_with_output_control_10 (
    .in_1(controlled_buffer_10_out), .in_3(in_20), .out_4(out_45), .in_2(or_1_out));
  D_flip_flop_with_output_control d_flip_flop_with_output_control_11 (
    .in_1(controlled_buffer_11_out), .in_3(in_20), .out_4(out_46), .in_2(or_1_out));
  D_flip_flop_with_output_control d_flip_flop_with_output_control_12 (
    .in_1(controlled_buffer_12_out), .in_3(in_20), .out_4(out_47), .in_2(or_1_out));
  D_flip_flop_with_output_control d_flip_flop_with_output_control_13 (
    .in_1(controlled_buffer_13_out), .in_3(in_20), .out_4(out_48), .in_2(or_1_out));
  D_flip_flop_with_output_control d_flip_flop_with_output_control_14 (
    .in_1(controlled_buffer_14_out), .in_3(in_20), .out_4(out_49), .in_2(or_1_out));
  D_flip_flop_with_output_control d_flip_flop_with_output_control_15 (
    .in_1(controlled_buffer_15_out), .in_3(in_20), .out_4(out_50), .in_2(or_1_out));
  D_flip_flop_with_output_control d_flip_flop_with_output_control_16 (
    .in_1(controlled_buffer_16_out), .in_3(in_20), .out_4(out_51), .in_2(or_1_out));
endmodule

module test_for_16_bit_registers (
  input  in_1,
  input  in_2,
  input  in_3,
  input  in_4,
  input  in_5,
  input  in_6,
  input  in_7,
  input  in_8,
  input  in_9,
  input  in_10,
  input  in_11,
  input  in_12,
  input  in_13,
  input  in_14,
  input  in_15,
  input  in_16,
  input  in_17,
  input  in_18,
  input  in_19,
  input  in_20,
  input  in_21,
  input  in_22,
  input  in_23,
  input  in_24,
  input  in_25,
  input  in_26,
  input  in_27,
  input  in_28,
  input  in_29,
  input  in_30,
  input  in_31,
  input  in_32,
  input  in_33,
  input  in_34,
  input  in_35,
  output out_36,
  output out_37,
  output out_38,
  output out_39,
  output out_40,
  output out_41,
  output out_42,
  output out_43,
  output out_44,
  output out_45,
  output out_46,
  output out_47,
  output out_48,
  output out_49,
  output out_50,
  output out_51
);

  _16_bit_registers u_16_bit_registers_1 (
    .in_1(in_1), .in_2(in_2), .in_3(in_3), .in_4(in_4), .in_5(in_5), .in_6(in_6), .in_7(in_7), .in_8(in_8),
    .in_9(in_9), .in_10(in_10), .in_11(in_11), .in_12(in_12), .in_13(in_13), .in_14(in_14), .in_15(in_15),
    .in_16(in_16), .in_17(in_17), .in_20(in_29), .in_19(in_20), .in_21(in_21), .in_22(in_22), .in_23(in_23),
    .in_24(in_24), .in_25(in_25), .in_26(in_26), .in_27(in_27), .in_28(in_28), .in_29(in_30), .in_30(in_31),
    .in_31(in_32), .in_32(in_33), .in_33(in_34), .in_34(in_35), .in_35(in_18), .out_36(out_36),
    .out_37(out_37), .out_38(out_38), .out_39(out_39), .out_40(out_40), .out_41(out_41), .out_42(out_42),
    .out_43(out_43), .out_44(out_44), .out_45(out_45), .out_46(out_46), .out_47(out_47), .out_48(out_48),
    .out_49(out_49), .out_50(out_50), .out_51(out_51), .in_18(in_19));
endmodule

module total_adder (
  input  a,
  input  b,
  input  Ci,
  output sum,
  output cout
);

  wire and_1_out, and_2_out, and_3_out, and_4_out, and_5_out, and_6_out, and_7_out, and_8_out, and_9_out,
       and_10_out, and_11_out, buffer_1_out, buffer_2_out, buffer_3_out, buffer_4_out, buffer_5_out,
       buffer_6_out, buffer_7_out, buffer_8_out, buffer_9_out, buffer_10_out, buffer_11_out, not_1_out,
       not_2_out, not_3_out, not_4_out, not_5_out, not_6_out, or_1_out, or_2_out, or_3_out, or_4_out;

  not not_1 (not_1_out, a);
  not not_2 (not_2_out, b);
  not not_3 (not_3_out, a);
  buf buffer_1 (buffer_1_out, b);
  buf buffer_2 (buffer_2_out, Ci);
  buf buffer_3 (buffer_3_out, a);
  not not_4 (not_4_out, b);
  buf buffer_4 (buffer_4_out, Ci);
  buf buffer_5 (buffer_5_out, a);
  buf buffer_6 (buffer_6_out, b);
  buf buffer_7 (buffer_7_out, Ci);
  and and_1 (and_1_out, b, Ci);
  and and_2 (and_2_out, a, Ci);
  buf buffer_8 (buffer_8_out, a);
  buf buffer_9 (buffer_9_out, b);
  and and_3 (and_3_out, not_1_out, not_2_out);
  and and_4 (and_4_out, not_3_out, buffer_1_out);
  not not_5 (not_5_out, buffer_2_out);
  and and_5 (and_5_out, buffer_3_out, not_4_out);
  not not_6 (not_6_out, buffer_4_out);
  and and_6 (and_6_out, buffer_5_out, buffer_6_out);
  buf buffer_10 (buffer_10_out, buffer_7_out);
  or or_1 (or_1_out, and_1_out, and_2_out);
  and and_7 (and_7_out, buffer_8_out, buffer_9_out);
  and and_8 (and_8_out, and_3_out, Ci);
  and and_9 (and_9_out, and_4_out, not_5_out);
  and and_10 (and_10_out, and_5_out, not_6_out);
  and and_11 (and_11_out, and_6_out, buffer_10_out);
  or or_2 (or_2_out, or_1_out, and_7_out);
  or or_3 (or_3_out, and_8_out, and_9_out);
  or or_4 (or_4_out, and_10_out, and_11_out);
  buf buffer_11 (buffer_11_out, or_2_out);
  or or_5 (sum, or_3_out, or_4_out);
  buf buffer_12 (cout, buffer_11_out);
endmodule

module _16_bit_total_adder (
  input  in_1,
  input  in_2,
  input  in_3,
  input  in_4,
  input  in_5,
  input  in_6,
  input  in_7,
  input  in_8,
  input  in_9,
  input  in_10,
  input  in_11,
  input  in_12,
  input  in_13,
  input  in_14,
  input  in_15,
  input  in_16,
  input  in_17,
  input  in_18,
  input  in_19,
  input  in_20,
  input  in_21,
  input  in_22,
  input  in_23,
  input  in_24,
  input  in_25,
  input  in_26,
  input  in_27,
  input  in_28,
  input  in_29,
  input  in_30,
  input  in_31,
  input  in_32,
  input  in_33,
  input  in_34,
  output out_35,
  output out_36,
  output out_37,
  output out_38,
  output out_39,
  output out_40,
  output out_41,
  output out_42,
  output out_43,
  output out_44,
  output out_45,
  output out_46,
  output out_47,
  output out_48,
  output out_49,
  output out_50,
  output out_51
);

  wire d_trigger_1_out_3, d_trigger_2_out_3, d_trigger_3_out_3, d_trigger_4_out_3, d_trigger_5_out_3,
       d_trigger_6_out_3, d_trigger_7_out_3, d_trigger_8_out_3, d_trigger_9_out_3, d_trigger_10_out_3,
       d_trigger_11_out_3, d_trigger_12_out_3, d_trigger_13_out_3, d_trigger_14_out_3, d_trigger_15_out_3,
       d_trigger_16_out_3, total_adder_1_cout, total_adder_1_sum, total_adder_2_cout, total_adder_2_sum,
       total_adder_3_cout, total_adder_3_sum, total_adder_4_cout, total_adder_4_sum, total_adder_5_cout,
       total_adder_5_sum, total_adder_6_cout, total_adder_6_sum, total_adder_7_cout, total_adder_7_sum,
       total_adder_8_cout, total_adder_8_sum, total_adder_9_cout, total_adder_9_sum, total_adder_10_cout,
       total_adder_10_sum, total_adder_11_cout, total_adder_11_sum, total_adder_12_cout, total_adder_12_sum,
       total_adder_13_cout, total_adder_13_sum, total_adder_14_cout, total_adder_14_sum, total_adder_15_cout,
       total_adder_15_sum, total_adder_16_sum;

  D_Trigger d_trigger_1 (.in_1(total_adder_1_sum), .in_2(in_33), .out_3(d_trigger_1_out_3));
  and and_1 (out_36, in_34, d_trigger_1_out_3);
  total_adder total_adder_1 (.a(in_1), .b(in_17), .Ci(1'b0), .sum(total_adder_1_sum), .cout(total_adder_1_cout));
  D_Trigger d_trigger_2 (.in_1(total_adder_2_sum), .in_2(in_33), .out_3(d_trigger_2_out_3));
  and and_2 (out_37, in_34, d_trigger_2_out_3);
  total_adder total_adder_2 (
    .a(in_2), .b(in_18), .Ci(total_adder_1_cout), .sum(total_adder_2_sum), .cout(total_adder_2_cout));
  D_Trigger d_trigger_3 (.in_1(total_adder_3_sum), .in_2(in_33), .out_3(d_trigger_3_out_3));
  and and_3 (out_38, in_34, d_trigger_3_out_3);
  total_adder total_adder_3 (
    .a(in_3), .b(in_19), .Ci(total_adder_2_cout), .sum(total_adder_3_sum), .cout(total_adder_3_cout));
  D_Trigger d_trigger_4 (.in_1(total_adder_5_sum), .in_2(in_33), .out_3(d_trigger_4_out_3));
  and and_4 (out_39, in_34, d_trigger_4_out_3);
  total_adder total_adder_4 (
    .a(in_5), .b(in_21), .Ci(total_adder_5_cout), .sum(total_adder_4_sum), .cout(total_adder_4_cout));
  total_adder total_adder_5 (
    .a(in_4), .b(in_20), .Ci(total_adder_3_cout), .sum(total_adder_5_sum), .cout(total_adder_5_cout));
  D_Trigger d_trigger_5 (.in_1(total_adder_4_sum), .in_2(in_33), .out_3(d_trigger_5_out_3));
  and and_5 (out_40, in_34, d_trigger_5_out_3);
  total_adder total_adder_6 (
    .a(in_6), .b(in_22), .Ci(total_adder_4_cout), .sum(total_adder_6_sum), .cout(total_adder_6_cout));
  D_Trigger d_trigger_6 (.in_1(total_adder_6_sum), .in_2(in_33), .out_3(d_trigger_6_out_3));
  and and_6 (out_41, in_34, d_trigger_6_out_3);
  total_adder total_adder_7 (
    .a(in_7), .b(in_23), .Ci(total_adder_6_cout), .sum(total_adder_7_sum), .cout(total_adder_7_cout));
  D_Trigger d_trigger_7 (.in_1(total_adder_7_sum), .in_2(in_33), .out_3(d_trigger_7_out_3));
  and and_7 (out_42, in_34, d_trigger_7_out_3);
  total_adder total_adder_8 (
    .a(in_8), .b(in_24), .Ci(total_adder_7_cout), .sum(total_adder_8_sum), .cout(total_adder_8_cout));
  D_Trigger d_trigger_8 (.in_1(total_adder_8_sum), .in_2(in_33), .out_3(d_trigger_8_out_3));
  and and_8 (out_43, in_34, d_trigger_8_out_3);
  and and_9 (out_44, in_34, d_trigger_9_out_3);
  total_adder total_adder_9 (
    .a(in_9), .b(in_25), .Ci(total_adder_8_cout), .sum(total_adder_9_sum), .cout(total_adder_9_cout));
  D_Trigger d_trigger_9 (.in_1(total_adder_9_sum), .in_2(in_33), .out_3(d_trigger_9_out_3));
  D_Trigger d_trigger_10 (.in_1(total_adder_10_sum), .in_2(in_33), .out_3(d_trigger_10_out_3));
  and and_10 (out_45, in_34, d_trigger_10_out_3);
  total_adder total_adder_10 (
    .a(in_10), .b(in_26), .Ci(total_adder_9_cout), .sum(total_adder_10_sum), .cout(total_adder_10_cout));
  D_Trigger d_trigger_11 (.in_1(total_adder_11_sum), .in_2(in_33), .out_3(d_trigger_11_out_3));
  and and_11 (out_46, in_34, d_trigger_11_out_3);
  total_adder total_adder_11 (
    .a(in_11), .b(in_27), .Ci(total_adder_10_cout), .sum(total_adder_11_sum), .cout(total_adder_11_cout));
  D_Trigger d_trigger_12 (.in_1(total_adder_12_sum), .in_2(in_33), .out_3(d_trigger_12_out_3));
  and and_12 (out_47, in_34, d_trigger_12_out_3);
  total_adder total_adder_12 (
    .a(in_12), .b(in_28), .Ci(total_adder_11_cout), .sum(total_adder_12_sum), .cout(total_adder_12_cout));
  total_adder total_adder_13 (
    .a(in_13), .b(in_29), .Ci(total_adder_12_cout), .sum(total_adder_13_sum), .cout(total_adder_13_cout));
  D_Trigger d_trigger_13 (.in_1(total_adder_13_sum), .in_2(in_33), .out_3(d_trigger_13_out_3));
  and and_13 (out_48, in_34, d_trigger_13_out_3);
  total_adder total_adder_14 (
    .a(in_14), .b(in_30), .Ci(total_adder_13_cout), .sum(total_adder_14_sum), .cout(total_adder_14_cout));
  D_Trigger d_trigger_14 (.in_1(total_adder_14_sum), .in_2(in_33), .out_3(d_trigger_14_out_3));
  and and_14 (out_49, in_34, d_trigger_14_out_3);
  total_adder total_adder_15 (
    .a(in_15), .b(in_30), .Ci(total_adder_14_cout), .sum(total_adder_15_sum), .cout(total_adder_15_cout));
  D_Trigger d_trigger_15 (.in_1(total_adder_15_sum), .in_2(in_33), .out_3(d_trigger_15_out_3));
  and and_15 (out_50, in_34, d_trigger_15_out_3);
  total_adder total_adder_16 (.a(in_16), .b(in_32), .Ci(total_adder_15_cout), .sum(total_adder_16_sum), .cout(out_35));
  D_Trigger d_trigger_16 (.in_1(total_adder_16_sum), .in_2(in_33), .out_3(d_trigger_16_out_3));
  and and_16 (out_51, in_34, d_trigger_16_out_3);

  assign in_31 = in_30;
endmodule

module parser (
  input  in_1,
  input  in_2,
  input  in_3,
  input  in_4,
  input  in_5,
  output out_6,
  output out_7,
  output out_8,
  output out_9,
  output out_10,
  output out_11,
  output out_12,
  output out_13,
  output out_14,
  output out_15,
  output out_16,
  output out_17
);

  wire multi_and_gates_1_out_5, multi_and_gates_2_out_5, multi_and_gates_3_out_5, multi_and_gates_4_out_5,
       multi_and_gates_5_out_5, multi_and_gates_6_out_5, multi_and_gates_7_out_5, multi_and_gates_8_out_5,
       multi_and_gates_9_out_5, multi_and_gates_10_out_5, multi_and_gates_11_out_5, multi_and_gates_12_out_5,
       not_1_out, not_2_out, not_3_out, not_4_out;

  not not_1 (not_1_out, in_1);
  not not_2 (not_2_out, in_2);
  not not_3 (not_3_out, in_3);
  not not_4 (not_4_out, in_4);
  Multi_AND_gates multi_and_gates_1 (
    .in_1(not_1_out), .in_2(not_2_out), .in_3(not_3_out), .in_4(not_4_out), .out_5(multi_and_gates_1_out_5));
  Multi_AND_gates multi_and_gates_2 (
    .in_1(in_1), .in_2(not_2_out), .in_3(not_3_out), .in_4(not_4_out), .out_5(multi_and_gates_2_out_5));
  Multi_AND_gates multi_and_gates_3 (
    .in_1(not_1_out), .in_2(in_2), .in_3(not_3_out), .in_4(not_4_out), .out_5(multi_and_gates_3_out_5));
  Multi_AND_gates multi_and_gates_4 (
    .in_1(in_1), .in_2(in_2), .in_3(not_3_out), .in_4(not_4_out), .out_5(multi_and_gates_4_out_5));
  Multi_AND_gates multi_and_gates_5 (
    .in_1(not_1_out), .in_2(not_2_out), .in_3(in_3), .in_4(not_4_out), .out_5(multi_and_gates_5_out_5));
  Multi_AND_gates multi_and_gates_6 (
    .in_1(in_1), .in_2(not_2_out), .in_3(in_3), .in_4(not_4_out), .out_5(multi_and_gates_6_out_5));
  Multi_AND_gates multi_and_gates_7 (
    .in_1(not_1_out), .in_2(in_2), .in_3(in_3), .in_4(not_4_out), .out_5(multi_and_gates_7_out_5));
  Multi_AND_gates multi_and_gates_8 (
    .in_1(in_1), .in_2(in_2), .in_3(in_3), .in_4(not_4_out), .out_5(multi_and_gates_8_out_5));
  Multi_AND_gates multi_and_gates_9 (
    .in_1(not_1_out), .in_2(not_2_out), .in_3(not_3_out), .in_4(in_4), .out_5(multi_and_gates_9_out_5));
  Multi_AND_gates multi_and_gates_10 (
    .in_1(in_1), .in_2(not_2_out), .in_3(not_3_out), .in_4(in_4), .out_5(multi_and_gates_10_out_5));
  Multi_AND_gates multi_and_gates_11 (
    .in_1(not_1_out), .in_2(in_2), .in_3(not_3_out), .in_4(in_4), .out_5(multi_and_gates_11_out_5));
  Multi_AND_gates multi_and_gates_12 (
    .in_1(in_1), .in_2(in_2), .in_3(not_3_out), .in_4(in_4), .out_5(multi_and_gates_12_out_5));
  and and_1 (out_6, multi_and_gates_1_out_5, in_5);
  and and_2 (out_7, multi_and_gates_2_out_5, in_5);
  and and_3 (out_8, multi_and_gates_3_out_5, in_5);
  and and_4 (out_9, multi_and_gates_4_out_5, in_5);
  and and_5 (out_10, multi_and_gates_5_out_5, in_5);
  and and_6 (out_11, multi_and_gates_6_out_5, in_5);
  and and_7 (out_12, multi_and_gates_7_out_5, in_5);
  and and_8 (out_13, multi_and_gates_8_out_5, in_5);
  and and_9 (out_14, multi_and_gates_9_out_5, in_5);
  and and_10 (out_15, multi_and_gates_10_out_5, in_5);
  and and_11 (out_16, multi_and_gates_11_out_5, in_5);
  and and_12 (out_17, multi_and_gates_12_out_5, in_5);
endmodule

module Multi_AND_gates (
  input  in_1,
  input  in_2,
  input  in_3,
  input  in_4,
  output out_5
);

  wire and_1_out, and_2_out;

  and and_1 (and_1_out, in_1, in_2);
  and and_2 (and_2_out, in_3, in_4);
  and and_3 (out_5, and_1_out, and_2_out);
endmodule
